# Fritzing sketch Prog_lab1 (saved by Fritzing 0.9.3b)
breadboards: 1

parts:
  LED1 = LED - 5mm [color="Red (633nm)" package="5 mm [THT]"]
  LED2 = smd LED [color="Yellow (595nm)" package="0603 [SMD]"]
  LED3 = smd LED [color="Green (555nm)" package="0603 [SMD]"]
  LED4 = smd LED [color="Green (555nm)" package="0603 [SMD]"]
  LED5 = smd LED [color="Red (633nm)" package="0603 [SMD]"]
  Part1 = Arduino Uno (Rev3)
  J1 = Basic Servo
  S1 = Pushbutton [package="[SMD]"]
  R1 = Resistor [tolerance=±5% resistance=220 package="1206 [SMD]"]
  R2 = Resistor [tolerance=±5% resistance=220 package="1206 [SMD]"]
  R3 = Resistor [tolerance=±5% resistance=10k package="1206 [SMD]"]
  R4 = Resistor [tolerance=±5% resistance=220 package="0402 [SMD]"]
  R6 = Resistor [tolerance=±5% resistance=220 package="0402 [SMD]"]
  R7 = Resistor [tolerance=±5% resistance=220 package="0402 [SMD]"]

nets:
  GND: LED1.cathode, LED2.cathode, LED3.cathode, LED4.cathode, LED5.cathode, Part1.GND, J1.gnd, R3.Pin_0
  N1: LED1.anode, R7.Pin_0
  N2: LED2.anode, R6.Pin_0
  N3: LED3.anode, R4.Pin_0
  N4: LED4.anode, R2.Pin_1
  N5: LED5.anode, R1.Pin_1
  N6: Part1.D8, R4.Pin_1
  N7: Part1.D9_PWM, R6.Pin_1
  N8: Part1.D12/MISO, S1.Pin_1, S1.Pin_2, R3.Pin_1
  N9: Part1.D7, J1.pulse
  N10: Part1.ioref, J1.vcc
  N11: S1.Pin_3, S1.Pin_4
