# Fritzing sketch fritz arduino zumo (saved by Fritzing 0.9.3b)
breadboards: 1

parts:
  Part1 = Arduino Uno (Rev3)
  J1 = Basic Servo
  hc-sr1 = hc-sr04
  Part2 = Bluetooth HC-05 Macho

nets:
  N1: Part1.A4/SDA, hc-sr1.Echo
  N2: Part1.A5/SCL, hc-sr1.Trig
  N3: Part1.D3_PWM, J1.pulse
  N4: Part1.D4, Part2.TXD
  N5: Part1.D5_PWM, Part2.RXD
  VCC: Part1.5V, J1.vcc, hc-sr1.VCC, Part2.VCC
  GND: Part1.GND, J1.gnd, hc-sr1.GND, Part2.GND
