# Fritzing sketch Øving 3 (saved by Fritzing 0.9.3b)
breadboards: 1

parts:
  Part1 = Arduino Uno (Rev3) - ICSP
  LED1 = LED - 3mm [color="Red (633nm)" package="3 mm [THT]"]
  R1 = Resistor [tolerance=±5% resistance=220 package="1206 [SMD]"]
  Part2 = Breakout Board for Electret Microphone

nets:
  N1: Part1.D0/RX, LED1.cathode
  N2: Part1.D2, Part2.GND
  3V3: Part1.3V3, Part2.VCC
  N3: Part1.5V, R1.Pin_0, Part2.AUD
  N4: LED1.anode, R1.Pin_1
